// Logisim project Nosferkcalc.circ as structural Verilog: 7 circuits, main circuit main
module main (
  input  A1,
  input  A2,
  input  A3,
  input  A4,
  input  A5,
  input  A6,
  input  A7,
  input  A8,
  input  A9,
  input  B1,
  input  b2,
  input  b3,
  input  b4,
  input  b5,
  input  b6,
  input  b7,
  input  b8,
  input  b9,
  input  MaisMenos
);

  wire n7404_1_pin2, n7404_1_pin8, n7404_1_pin10, n7404_1_pin12, n7404_2_pin2, n7404_2_pin4, n7404_2_pin6,
       n7404_2_pin12, n7404_3_pin2, n7404_3_pin8, n7404_3_pin10, n7404_3_pin12, n7404_5_pin3, n7404_5_pin4,
       n7404_5_pin6, n7404_5_pin8, n7404_5_pin10, n7404_6_pin2, n7404_6_pin6, n7404_6_pin10, n7404_7_pin12,
       n7408_1_pin8, n7408_2_pin1, n7408_2_pin2, n7408_2_pin3, n7408_2_pin5, n7408_2_pin6, n7408_2_pin8,
       n7408_2_pin11, n7408_2_pin12, n7408_2_pin13, n7408_3_pin1, n7408_3_pin3, n7408_3_pin4, n7408_3_pin6,
       n7408_3_pin8, n7408_3_pin9, n7408_3_pin10, n7408_4_pin1, n7408_4_pin3, n7408_5_pin3, n7408_5_pin8,
       n7408_5_pin9, n7408_5_pin11, n7408_5_pin12, n7408_5_pin13, n7408_6_pin8, n7408_6_pin9, n7408_6_pin11,
       n7408_7_pin3, n7408_7_pin6, n7408_7_pin8, n7408_7_pin11, n7408_8_pin3, n7408_8_pin4, n7408_8_pin6,
       n7408_8_pin8, n7408_8_pin9, n7408_8_pin11, n7408_9_pin6, n7408_10_pin3, n7408_10_pin11, n7432_1_pin1,
       n7432_1_pin6, n7432_1_pin8, n7432_1_pin9, n7432_2_pin3, n7432_2_pin11, n7432_3_pin3, n7432_3_pin5,
       n7432_3_pin6, n7432_3_pin11, n7432_4_pin1, n7432_4_pin3, n7432_4_pin6, n7432_4_pin8, n7432_4_pin9,
       n7432_6_pin3, n7432_6_pin11, n7432_7_pin3, n7432_7_pin5, n7432_7_pin6, n7432_7_pin11, n7432_8_pin1,
       n7432_8_pin3, n7432_8_pin6, n7432_8_pin8, n7432_9_pin8, n7432_9_pin11, n7432_10_pin2, n7432_10_pin4,
       n7432_10_pin5, n7432_10_pin6, n7432_10_pin8, n7432_10_pin11, n7432_11_pin6, n7432_11_pin11,
       n7432_12_pin3, n7432_13_pin6, n7432_13_pin11, n7432_14_pin1, n7432_14_pin2, n7432_14_pin3,
       n7432_14_pin5, n7432_14_pin6, n7432_14_pin11, n7432_14_pin12, n7432_15_pin11, n7432_15_pin13,
       n7486_1_pin3, n74181_1_p1, n74181_1_p2, n74181_1_p9, n74181_1_p10, n74181_1_p11, n74181_1_p14;

  _7432 u_7432_1 (
    .pin1(n7432_1_pin1), .pin2(b7), .pin5(b9), .pin6(n7432_1_pin6), .pin10(b7), .pin9(n7432_1_pin9),
    .pin8(n7432_1_pin8));  // open: pin3, pin4, pin13, pin12, pin11
  _7432 u_7432_2 (
    .pin1(B1), .pin2(b3), .pin3(n7432_2_pin3), .pin4(n7432_2_pin3), .pin5(b5), .pin6(n7432_1_pin1),
    .pin13(b2), .pin12(b3), .pin11(n7432_2_pin11), .pin10(n7432_2_pin11), .pin9(b6), .pin8(n7432_1_pin9));
  _7432 u_7432_3 (
    .pin1(b6), .pin2(b7), .pin3(n7432_3_pin3), .pin4(n7432_3_pin3), .pin5(n7432_3_pin5), .pin6(n7432_3_pin6),
    .pin13(b9), .pin12(b8), .pin11(n7432_3_pin11), .pin10(b4), .pin9(b5), .pin8(n7432_3_pin5));
  _7432 u_7432_4 (
    .pin1(n7432_4_pin1), .pin2(A7), .pin3(n7432_4_pin3), .pin4(n7432_4_pin3), .pin5(A9), .pin6(n7432_4_pin6),
    .pin10(A7), .pin9(n7432_4_pin9), .pin8(n7432_4_pin8));  // open: pin13, pin12, pin11
  _7432 u_7432_5 ();  // open: pin1, pin2, pin3, pin4, pin5, pin6, pin13, pin12, pin11, pin10, pin9, pin8
  _7432 u_7432_6 (
    .pin1(A1), .pin2(A3), .pin3(n7432_6_pin3), .pin4(n7432_6_pin3), .pin5(A5), .pin6(n7432_4_pin1),
    .pin13(A2), .pin12(A3), .pin11(n7432_6_pin11), .pin10(n7432_6_pin11), .pin9(A6), .pin8(n7432_4_pin9));
  _7432 u_7432_7 (
    .pin1(A6), .pin2(A7), .pin3(n7432_7_pin3), .pin4(n7432_7_pin3), .pin5(n7432_7_pin5), .pin6(n7432_7_pin6),
    .pin13(A9), .pin12(A8), .pin11(n7432_7_pin11), .pin10(A4), .pin9(A5), .pin8(n7432_7_pin5));
  _7404 u_7404_1 (
    .pin1(n7432_4_pin6), .pin2(n7404_1_pin2), .pin13(n7432_7_pin11), .pin12(n7404_1_pin12),
    .pin11(n7432_7_pin6), .pin10(n7404_1_pin10), .pin9(n7432_4_pin8), .pin8(n7404_1_pin8));  // open: pin3, pin4, pin5, pin6
  _7404 u_7404_2 (
    .pin1(n7432_1_pin6), .pin2(n7404_2_pin2), .pin3(n7432_1_pin8), .pin4(n7404_2_pin4), .pin5(n7432_3_pin6),
    .pin6(n7404_2_pin6), .pin13(n7432_3_pin11), .pin12(n7404_2_pin12));  // open: pin11, pin10, pin9, pin8
  // _74181 #(.ShowInternalStructure("true")) 74181_1: pin names not known; wires that end beside it: n74181_1_p1, n74181_1_p2, n7404_2_pin12, n7404_1_pin12, n7404_2_pin6, n7404_1_pin10, n7404_2_pin4, n7404_1_pin8, n74181_1_p9, n74181_1_p10, n74181_1_p11, 1'b0, MaisMenos, n74181_1_p14, MaisMenos, MaisMenos, n74181_1_p14, n7404_1_pin2, n7404_2_pin2
  _7404 u_7404_3 (
    .pin1(n74181_1_p11), .pin2(n7404_3_pin2), .pin3(MaisMenos), .pin4(n74181_1_p14), .pin13(n74181_1_p1),
    .pin12(n7404_3_pin12), .pin11(n74181_1_p9), .pin10(n7404_3_pin10), .pin9(n74181_1_p10),
    .pin8(n7404_3_pin8));  // open: pin5, pin6
  _7408 u_7408_1 (
    .pin10(n74181_1_p2), .pin9(n74181_1_p14), .pin8(n7408_1_pin8));  // open: pin1, pin2, pin3, pin4, pin5, pin6, pin13, pin12, pin11
  _7408 u_7408_2 (
    .pin1(n7408_2_pin1), .pin2(n7408_2_pin2), .pin3(n7408_2_pin3), .pin4(n7408_2_pin3), .pin5(n7408_2_pin5),
    .pin6(n7408_2_pin6), .pin13(n7408_2_pin13), .pin12(n7408_2_pin12), .pin11(n7408_2_pin11),
    .pin10(n7408_2_pin11), .pin9(n7408_2_pin6), .pin8(n7408_2_pin8));
  _7404 u_7404_4 (
    .pin1(n7404_3_pin10), .pin2(n7408_2_pin12), .pin3(n7404_3_pin12), .pin4(n7408_2_pin13),
    .pin13(n7404_3_pin2), .pin12(n7408_2_pin2), .pin11(n7404_3_pin8), .pin10(n7408_2_pin1),
    .pin9(n7408_1_pin8), .pin8(n7408_2_pin5));  // open: pin5, pin6
  _7408 u_7408_3 (
    .pin1(n7408_3_pin1), .pin2(n7404_3_pin10), .pin3(n7408_3_pin3), .pin4(n7408_3_pin4),
    .pin5(n7404_3_pin12), .pin6(n7408_3_pin6), .pin10(n7408_3_pin10), .pin9(n7408_3_pin9), .pin8(n7408_3_pin8));  // open: pin13, pin12, pin11
  _7432 u_7432_8 (
    .pin1(n7432_8_pin1), .pin2(n7408_1_pin8), .pin3(n7432_8_pin3), .pin4(n7432_8_pin3), .pin5(n7404_3_pin2),
    .pin6(n7432_8_pin6), .pin13(n7404_3_pin10), .pin12(n7404_3_pin8), .pin11(n7408_3_pin4),
    .pin10(n7408_1_pin8), .pin9(n7408_3_pin6), .pin8(n7432_8_pin8));
  _7408 u_7408_4 (
    .pin1(n7408_4_pin1), .pin2(n7404_3_pin2), .pin3(n7408_4_pin3));  // open: pin4, pin5, pin6, pin13, pin12, pin11, pin10, pin9, pin8
  _7408 u_7408_5 (
    .pin1(n7408_1_pin8), .pin2(n7408_2_pin2), .pin3(n7408_5_pin3), .pin4(n7404_3_pin12),
    .pin5(n7404_3_pin10), .pin6(n7408_4_pin1), .pin13(n7408_5_pin13), .pin12(n7408_5_pin12),
    .pin11(n7408_5_pin11), .pin10(n7404_3_pin8), .pin9(n7408_5_pin9), .pin8(n7408_5_pin8));
  _7404 u_7404_5 (
    .pin1(n7404_3_pin2), .pin2(n7408_3_pin9), .pin3(n7404_5_pin3), .pin4(n7404_5_pin4), .pin5(n7432_8_pin8),
    .pin6(n7404_5_pin6), .pin11(n7404_3_pin10), .pin10(n7404_5_pin10), .pin9(n7408_1_pin8),
    .pin8(n7404_5_pin8));  // open: pin13, pin12
  _7432 u_7432_9 (
    .pin4(n7408_4_pin3), .pin5(n7408_5_pin3), .pin6(n7408_5_pin9), .pin13(n7408_2_pin8),
    .pin12(n7408_5_pin8), .pin11(n7432_9_pin11), .pin10(n7432_9_pin11), .pin9(n7408_5_pin11),
    .pin8(n7432_9_pin8));  // open: pin1, pin2, pin3
  _7432 u_7432_10 (
    .pin1(n7404_5_pin10), .pin2(n7432_10_pin2), .pin3(n7408_3_pin10), .pin4(n7432_10_pin4),
    .pin5(n7432_10_pin5), .pin6(n7432_10_pin6), .pin13(n7432_10_pin2), .pin12(n7404_5_pin4),
    .pin11(n7432_10_pin11), .pin10(n7404_3_pin12), .pin9(n7432_10_pin6), .pin8(n7432_10_pin8));
  _7486 u_7486_1 (
    .pin1(n7404_3_pin10), .pin2(n7404_3_pin8), .pin3(n7486_1_pin3), .pin13(n7404_3_pin12),
    .pin12(n7404_3_pin8), .pin11(n7432_10_pin2), .pin10(n7404_3_pin10), .pin9(n7404_3_pin2),
    .pin8(n7404_5_pin3));  // open: pin4, pin5, pin6
  _7486 u_7486_2 (
    .pin13(n7404_3_pin12), .pin12(n7404_3_pin8), .pin11(n7408_5_pin12), .pin10(n7404_3_pin10),
    .pin9(n7404_3_pin2), .pin8(n7408_5_pin13));  // open: pin1, pin2, pin3, pin4, pin5, pin6
  _7404 u_7404_6 (
    .pin1(n7486_1_pin3), .pin2(n7404_6_pin2), .pin5(n7404_3_pin10), .pin6(n7404_6_pin6),
    .pin11(n7404_3_pin12), .pin10(n7404_6_pin10), .pin9(n7404_3_pin8), .pin8(n7408_3_pin1));  // open: pin3, pin4, pin13, pin12
  _7408 u_7408_6 (
    .pin1(n7404_5_pin8), .pin2(n7408_3_pin1), .pin3(n7432_10_pin4), .pin4(n7404_3_pin8),
    .pin5(n7404_5_pin10), .pin6(n7432_10_pin5), .pin13(n7408_3_pin9), .pin12(n7432_10_pin8),
    .pin11(n7408_6_pin11), .pin10(n7404_3_pin2), .pin9(n7408_6_pin9), .pin8(n7408_6_pin8));
  _7408 u_7408_7 (
    .pin1(n7404_6_pin6), .pin2(n7408_3_pin1), .pin3(n7408_7_pin3), .pin4(n7404_6_pin10), .pin5(n7404_6_pin6),
    .pin6(n7408_7_pin6), .pin13(n7404_3_pin12), .pin12(n7404_3_pin8), .pin11(n7408_7_pin11),
    .pin10(n7404_6_pin10), .pin9(n7404_3_pin10), .pin8(n7408_7_pin8));
  _7432 u_7432_11 (
    .pin1(n7432_10_pin2), .pin2(n7404_5_pin10), .pin3(n7408_6_pin9), .pin4(n7408_7_pin11),
    .pin5(n7408_7_pin8), .pin6(n7432_11_pin6), .pin13(n7408_6_pin8), .pin12(n7408_6_pin11),
    .pin11(n7432_11_pin11), .pin10(n7408_7_pin3), .pin9(n7432_11_pin6), .pin8(n7432_8_pin1));
  _7404 u_7404_7 (
    .pin13(n7404_3_pin2), .pin12(n7404_7_pin12));  // open: pin1, pin2, pin3, pin4, pin5, pin6, pin11, pin10, pin9, pin8
  _7432 u_7432_12 (
    .pin1(n7432_10_pin11), .pin2(n7408_1_pin8), .pin3(n7432_12_pin3));  // open: pin4, pin5, pin6, pin13, pin12, pin11, pin10, pin9, pin8
  _7408 u_7408_8 (
    .pin1(n7408_6_pin9), .pin2(n7408_3_pin9), .pin3(n7408_8_pin3), .pin4(n7408_8_pin4), .pin5(n7404_3_pin2),
    .pin6(n7408_8_pin6), .pin13(n7408_7_pin6), .pin12(n7404_3_pin8), .pin11(n7408_8_pin11),
    .pin10(n7404_3_pin12), .pin9(n7408_8_pin9), .pin8(n7408_8_pin8));
  _7432 u_7432_13 (
    .pin1(n7404_3_pin10), .pin2(n7408_3_pin1), .pin3(n7408_8_pin9), .pin4(n7408_3_pin3),
    .pin5(n7408_8_pin11), .pin6(n7432_13_pin6), .pin13(n7408_8_pin6), .pin12(n7408_8_pin3),
    .pin11(n7432_13_pin11), .pin10(n7432_13_pin6), .pin9(n7408_8_pin8), .pin8(n7408_8_pin4));
  _7432 u_7432_14 (
    .pin1(n7432_14_pin1), .pin2(n7432_14_pin2), .pin3(n7432_14_pin3), .pin4(n7432_10_pin2),
    .pin5(n7432_14_pin5), .pin6(n7432_14_pin6), .pin13(n7408_8_pin6), .pin12(n7432_14_pin12),
    .pin11(n7432_14_pin11), .pin10(n7408_1_pin8), .pin9(n7404_3_pin10), .pin8(n7432_14_pin5));
  _7408 u_7408_9 (
    .pin1(n7432_8_pin3), .pin2(n7408_3_pin9), .pin3(n7432_14_pin2), .pin4(n7404_6_pin10),
    .pin5(n7408_3_pin1), .pin6(n7408_9_pin6), .pin13(n7408_3_pin9), .pin12(n7432_14_pin6),
    .pin11(n7432_14_pin12), .pin9(n7432_14_pin5));  // open: pin10, pin8
  _7_Segment_Display #(.decimalPoint("false")) u_7_segment_display_1 (
    .g(1'b0), .f(n7404_5_pin6), .a(n7404_5_pin6), .b(1'b1), .e(n7404_5_pin6), .d(n7404_5_pin6), .c(1'b1));
  _7432 u_7432_15 (
    .pin13(n7432_15_pin13), .pin12(n7432_14_pin3), .pin11(n7432_15_pin11));  // open: pin1, pin2, pin3, pin4, pin5, pin6, pin10, pin9, pin8
  _7408 u_7408_10 (
    .pin1(n7408_9_pin6), .pin2(n7404_3_pin10), .pin3(n7408_10_pin3), .pin4(n7408_10_pin3),
    .pin5(n7404_3_pin2), .pin6(n7432_14_pin1), .pin13(n7404_3_pin2), .pin12(n7404_3_pin12),
    .pin11(n7408_10_pin11), .pin10(n7408_10_pin11), .pin9(n7404_6_pin2), .pin8(n7432_15_pin13));
  LED led_1 (.in(n7404_3_pin2));
  LED led_2 (.in(n7432_9_pin8));
  LED led_3 (.in(n7404_7_pin12));
  _7_Segment_Display #(.decimalPoint("false")) u_7_segment_display_2 (
    .g(n7432_14_pin11), .f(n7432_15_pin11), .a(n7432_12_pin3), .b(n7432_11_pin11), .e(n7408_3_pin8),
    .d(n7432_13_pin11), .c(n7432_8_pin6));

  // Notes on the sheet:
  //   X1
  //   X2
  //   X3
  //   X4
  //   X1
  //   X2
  //   X3
  //   X4
  //   Multiplo de 3
  //   impar
  //   par
endmodule

module Blocos (
  input  A1,
  input  A2,
  input  A3,
  input  A4,
  input  A5,
  input  A6,
  input  A7,
  input  A8,
  input  A9,
  input  B1,
  input  b2,
  input  b3,
  input  b4,
  input  b5,
  input  b6,
  input  b7,
  input  b8,
  input  b9,
  input  MaisMenos,
  output x1,
  output x2,
  output x3,
  output x4,
  output m1,
  output y1,
  output y2,
  output y3,
  output y4
);

  wire n7432_1_pin1, n7432_1_pin9, n7432_2_pin3, n7432_2_pin11, n7432_3_pin3, n7432_3_pin5, n7432_4_pin1,
       n7432_4_pin3, n7432_4_pin9, n7432_6_pin3, n7432_6_pin11, n7432_7_pin3, n7432_7_pin5;

  _7432 u_7432_1 (
    .pin1(n7432_1_pin1), .pin2(b7), .pin5(b9), .pin6(y4), .pin10(b7), .pin9(n7432_1_pin9), .pin8(y3));  // open: pin3, pin4, pin13, pin12, pin11
  _7432 u_7432_2 (
    .pin1(B1), .pin2(b3), .pin3(n7432_2_pin3), .pin4(n7432_2_pin3), .pin5(b5), .pin6(n7432_1_pin1),
    .pin13(b2), .pin12(b3), .pin11(n7432_2_pin11), .pin10(n7432_2_pin11), .pin9(b6), .pin8(n7432_1_pin9));
  _7432 u_7432_3 (
    .pin1(b6), .pin2(b7), .pin3(n7432_3_pin3), .pin4(n7432_3_pin3), .pin5(n7432_3_pin5), .pin6(y2),
    .pin13(b9), .pin12(b8), .pin11(y1), .pin10(b4), .pin9(b5), .pin8(n7432_3_pin5));
  _7432 u_7432_4 (
    .pin1(n7432_4_pin1), .pin2(A7), .pin3(n7432_4_pin3), .pin4(n7432_4_pin3), .pin5(A9), .pin6(x4),
    .pin10(A7), .pin9(n7432_4_pin9), .pin8(x3));  // open: pin13, pin12, pin11
  _7432 u_7432_5 ();  // open: pin1, pin2, pin3, pin4, pin5, pin6, pin13, pin12, pin11, pin10, pin9, pin8
  _7432 u_7432_6 (
    .pin1(A1), .pin2(A3), .pin3(n7432_6_pin3), .pin4(n7432_6_pin3), .pin5(A5), .pin6(n7432_4_pin1),
    .pin13(A2), .pin12(A3), .pin11(n7432_6_pin11), .pin10(n7432_6_pin11), .pin9(A6), .pin8(n7432_4_pin9));
  _7432 u_7432_7 (
    .pin1(A6), .pin2(A7), .pin3(n7432_7_pin3), .pin4(n7432_7_pin3), .pin5(n7432_7_pin5), .pin6(x2),
    .pin13(A9), .pin12(A8), .pin11(x1), .pin10(A4), .pin9(A5), .pin8(n7432_7_pin5));

  assign m1 = MaisMenos;

  // Notes on the sheet:
  //   X1
  //   X2
  //   X3
  //   X4
  //   X1
  //   X2
  //   X3
  //   X4
endmodule

module Ali (
  input  q1,
  input  q2,
  input  q3,
  input  q4,
  input  m,
  input  w1,
  input  w2,
  input  w3,
  input  w4,
  output s1,
  output s2,
  output s3,
  output s4,
  output s5
);

  wire n7404_1_pin2, n7404_1_pin8, n7404_1_pin10, n7404_1_pin12, n7404_2_pin2, n7404_2_pin4, n7404_2_pin6,
       n7404_2_pin12, n74181_1_p1, n74181_1_p2, n74181_1_p9, n74181_1_p10, n74181_1_p11, n74181_1_p14;

  _7404 u_7404_1 (
    .pin1(q4), .pin2(n7404_1_pin2), .pin13(q1), .pin12(n7404_1_pin12), .pin11(q2), .pin10(n7404_1_pin10),
    .pin9(q3), .pin8(n7404_1_pin8));  // open: pin3, pin4, pin5, pin6
  _7404 u_7404_2 (
    .pin1(w4), .pin2(n7404_2_pin2), .pin3(w3), .pin4(n7404_2_pin4), .pin5(w2), .pin6(n7404_2_pin6),
    .pin13(w1), .pin12(n7404_2_pin12));  // open: pin11, pin10, pin9, pin8
  // _74181 #(.ShowInternalStructure("true")) 74181_1: pin names not known; wires that end beside it: n74181_1_p1, n74181_1_p2, n7404_2_pin12, n7404_1_pin12, n7404_2_pin6, n7404_1_pin10, n7404_2_pin4, n7404_1_pin8, n74181_1_p9, n74181_1_p10, n74181_1_p11, 1'b0, m, n74181_1_p14, m, m, n74181_1_p14, n7404_1_pin2, n7404_2_pin2
  _7404 u_7404_3 (
    .pin1(n74181_1_p11), .pin2(s5), .pin3(m), .pin4(n74181_1_p14), .pin13(n74181_1_p1), .pin12(s2),
    .pin11(n74181_1_p9), .pin10(s3), .pin9(n74181_1_p10), .pin8(s4));  // open: pin5, pin6
  _7408 u_7408_1 (
    .pin10(n74181_1_p2), .pin9(n74181_1_p14), .pin8(s1));  // open: pin1, pin2, pin3, pin4, pin5, pin6, pin13, pin12, pin11

  // Notes on the sheet:
  //   X1
  //   X2
  //   X3
  //   X4
  //   X1
  //   X2
  //   X3
  //   X4
endmodule

module Mult3 (
  input  in_1,
  input  in_2,
  input  in_3,
  input  in_4,
  input  in_5,
  output out_6
);

  wire n7408_1_pin1, n7408_1_pin2, n7408_1_pin3, n7408_1_pin5, n7408_1_pin6, n7408_1_pin8, n7408_1_pin11,
       n7408_1_pin12, n7408_1_pin13, n7408_2_pin1, n7408_2_pin3, n7408_3_pin12, n7408_3_pin13, n7432_1_pin5,
       n7432_1_pin6, n7432_1_pin9, n7432_1_pin11, n7432_1_pin12;

  _7408 u_7408_1 (
    .pin1(n7408_1_pin1), .pin2(n7408_1_pin2), .pin3(n7408_1_pin3), .pin4(n7408_1_pin3), .pin5(n7408_1_pin5),
    .pin6(n7408_1_pin6), .pin13(n7408_1_pin13), .pin12(n7408_1_pin12), .pin11(n7408_1_pin11),
    .pin10(n7408_1_pin11), .pin9(n7408_1_pin6), .pin8(n7408_1_pin8));
  _7404 u_7404_1 (
    .pin1(in_3), .pin2(n7408_1_pin12), .pin3(in_2), .pin4(n7408_1_pin13), .pin13(in_5), .pin12(n7408_1_pin2),
    .pin11(in_4), .pin10(n7408_1_pin1), .pin9(in_1), .pin8(n7408_1_pin5));  // open: pin5, pin6
  _7408 u_7408_2 (
    .pin1(n7408_2_pin1), .pin2(in_5), .pin3(n7408_2_pin3));  // open: pin4, pin5, pin6, pin13, pin12, pin11, pin10, pin9, pin8
  _7432 u_7432_1 (
    .pin4(n7408_2_pin3), .pin5(n7432_1_pin5), .pin6(n7432_1_pin6), .pin13(n7408_1_pin8),
    .pin12(n7432_1_pin12), .pin11(n7432_1_pin11), .pin10(n7432_1_pin11), .pin9(n7432_1_pin9), .pin8(out_6));  // open: pin1, pin2, pin3
  _7408 u_7408_3 (
    .pin1(in_1), .pin2(n7408_1_pin2), .pin3(n7432_1_pin5), .pin4(in_2), .pin5(in_3), .pin6(n7408_2_pin1),
    .pin13(n7408_3_pin13), .pin12(n7408_3_pin12), .pin11(n7432_1_pin9), .pin10(in_4), .pin9(n7432_1_pin6),
    .pin8(n7432_1_pin12));
  _7486 u_7486_1 (
    .pin13(in_2), .pin12(in_4), .pin11(n7408_3_pin12), .pin10(in_3), .pin9(in_5), .pin8(n7408_3_pin13));  // open: pin1, pin2, pin3, pin4, pin5, pin6
endmodule

module decodificador (
  input  e1,
  input  e2,
  input  e3,
  input  e4,
  input  e5,
  output f4,
  output f3,
  output f2,
  output f1,
  output g1,
  output g2,
  output g3,
  output g4,
  output f5,
  output g5,
  output g6,
  output g7,
  output f7,
  output f6
);

  wire n7404_1_pin3, n7404_1_pin4, n7404_1_pin8, n7404_1_pin10, n7404_2_pin2, n7404_2_pin6, n7404_2_pin10,
       n7408_1_pin1, n7408_1_pin3, n7408_1_pin4, n7408_1_pin6, n7408_1_pin9, n7408_1_pin10, n7408_2_pin8,
       n7408_2_pin9, n7408_2_pin11, n7408_3_pin3, n7408_3_pin6, n7408_3_pin8, n7408_3_pin11, n7408_4_pin3,
       n7408_4_pin4, n7408_4_pin6, n7408_4_pin8, n7408_4_pin9, n7408_4_pin11, n7408_5_pin6, n7408_6_pin3,
       n7408_6_pin11, n7432_1_pin1, n7432_1_pin3, n7432_1_pin8, n7432_2_pin2, n7432_2_pin4, n7432_2_pin5,
       n7432_2_pin6, n7432_2_pin8, n7432_2_pin11, n7432_3_pin6, n7432_5_pin6, n7432_6_pin1, n7432_6_pin2,
       n7432_6_pin3, n7432_6_pin5, n7432_6_pin6, n7432_6_pin12, n7432_7_pin13, n7486_1_pin3;

  _7408 u_7408_1 (
    .pin1(n7408_1_pin1), .pin2(e3), .pin3(n7408_1_pin3), .pin4(n7408_1_pin4), .pin5(e2), .pin6(n7408_1_pin6),
    .pin10(n7408_1_pin10), .pin9(n7408_1_pin9), .pin8(g5));  // open: pin13, pin12, pin11
  _7432 u_7432_1 (
    .pin1(n7432_1_pin1), .pin2(e1), .pin3(n7432_1_pin3), .pin4(n7432_1_pin3), .pin5(e5), .pin6(g7),
    .pin13(e3), .pin12(e4), .pin11(n7408_1_pin4), .pin10(e1), .pin9(n7408_1_pin6), .pin8(n7432_1_pin8));
  _7404 u_7404_1 (
    .pin1(e5), .pin2(n7408_1_pin9), .pin3(n7404_1_pin3), .pin4(n7404_1_pin4), .pin5(n7432_1_pin8), .pin6(f2),
    .pin11(e3), .pin10(n7404_1_pin10), .pin9(e1), .pin8(n7404_1_pin8));  // open: pin13, pin12
  _7432 u_7432_2 (
    .pin1(n7404_1_pin10), .pin2(n7432_2_pin2), .pin3(n7408_1_pin10), .pin4(n7432_2_pin4),
    .pin5(n7432_2_pin5), .pin6(n7432_2_pin6), .pin13(n7432_2_pin2), .pin12(n7404_1_pin4),
    .pin11(n7432_2_pin11), .pin10(e2), .pin9(n7432_2_pin6), .pin8(n7432_2_pin8));
  _7486 u_7486_1 (
    .pin1(e3), .pin2(e4), .pin3(n7486_1_pin3), .pin13(e2), .pin12(e4), .pin11(n7432_2_pin2), .pin10(e3),
    .pin9(e5), .pin8(n7404_1_pin3));  // open: pin4, pin5, pin6
  _7404 u_7404_2 (
    .pin1(n7486_1_pin3), .pin2(n7404_2_pin2), .pin5(e3), .pin6(n7404_2_pin6), .pin11(e2),
    .pin10(n7404_2_pin10), .pin9(e4), .pin8(n7408_1_pin1));  // open: pin3, pin4, pin13, pin12
  _7408 u_7408_2 (
    .pin1(n7404_1_pin8), .pin2(n7408_1_pin1), .pin3(n7432_2_pin4), .pin4(e4), .pin5(n7404_1_pin10),
    .pin6(n7432_2_pin5), .pin13(n7408_1_pin9), .pin12(n7432_2_pin8), .pin11(n7408_2_pin11), .pin10(e5),
    .pin9(n7408_2_pin9), .pin8(n7408_2_pin8));
  _7408 u_7408_3 (
    .pin1(n7404_2_pin6), .pin2(n7408_1_pin1), .pin3(n7408_3_pin3), .pin4(n7404_2_pin10), .pin5(n7404_2_pin6),
    .pin6(n7408_3_pin6), .pin13(e2), .pin12(e4), .pin11(n7408_3_pin11), .pin10(n7404_2_pin10), .pin9(e3),
    .pin8(n7408_3_pin8));
  _7432 u_7432_3 (
    .pin1(n7432_2_pin2), .pin2(n7404_1_pin10), .pin3(n7408_2_pin9), .pin4(n7408_3_pin11),
    .pin5(n7408_3_pin8), .pin6(n7432_3_pin6), .pin13(n7408_2_pin8), .pin12(n7408_2_pin11), .pin11(g4),
    .pin10(n7408_3_pin3), .pin9(n7432_3_pin6), .pin8(n7432_1_pin1));
  _7432 u_7432_4 (
    .pin1(n7432_2_pin11), .pin2(e1), .pin3(g3));  // open: pin4, pin5, pin6, pin13, pin12, pin11, pin10, pin9, pin8
  _7408 u_7408_4 (
    .pin1(n7408_2_pin9), .pin2(n7408_1_pin9), .pin3(n7408_4_pin3), .pin4(n7408_4_pin4), .pin5(e5),
    .pin6(n7408_4_pin6), .pin13(n7408_3_pin6), .pin12(e4), .pin11(n7408_4_pin11), .pin10(e2),
    .pin9(n7408_4_pin9), .pin8(n7408_4_pin8));
  _7432 u_7432_5 (
    .pin1(e3), .pin2(n7408_1_pin1), .pin3(n7408_4_pin9), .pin4(n7408_1_pin3), .pin5(n7408_4_pin11),
    .pin6(n7432_5_pin6), .pin13(n7408_4_pin6), .pin12(n7408_4_pin3), .pin11(g6), .pin10(n7432_5_pin6),
    .pin9(n7408_4_pin8), .pin8(n7408_4_pin4));
  _7432 u_7432_6 (
    .pin1(n7432_6_pin1), .pin2(n7432_6_pin2), .pin3(n7432_6_pin3), .pin4(n7432_2_pin2), .pin5(n7432_6_pin5),
    .pin6(n7432_6_pin6), .pin13(n7408_4_pin6), .pin12(n7432_6_pin12), .pin11(g1), .pin10(e1), .pin9(e3),
    .pin8(n7432_6_pin5));
  _7408 u_7408_5 (
    .pin1(n7432_1_pin3), .pin2(n7408_1_pin9), .pin3(n7432_6_pin2), .pin4(n7404_2_pin10), .pin5(n7408_1_pin1),
    .pin6(n7408_5_pin6), .pin13(n7408_1_pin9), .pin12(n7432_6_pin6), .pin11(n7432_6_pin12),
    .pin9(n7432_6_pin5));  // open: pin10, pin8
  _7432 u_7432_7 (
    .pin13(n7432_7_pin13), .pin12(n7432_6_pin3), .pin11(g2));  // open: pin1, pin2, pin3, pin4, pin5, pin6, pin10, pin9, pin8
  _7408 u_7408_6 (
    .pin1(n7408_5_pin6), .pin2(e3), .pin3(n7408_6_pin3), .pin4(n7408_6_pin3), .pin5(e5), .pin6(n7432_6_pin1),
    .pin13(e5), .pin12(e2), .pin11(n7408_6_pin11), .pin10(n7408_6_pin11), .pin9(n7404_2_pin2),
    .pin8(n7432_7_pin13));

  assign f1 = 1'b0;
  assign f3 = f2;
  assign f4 = 1'b1;
  assign f5 = f2;
  assign f6 = f2;
  assign f7 = 1'b1;
endmodule

module Bloco (
  input  in_1,
  input  in_2,
  input  in_3,
  input  in_4,
  input  in_5,
  input  in_6,
  input  in_7,
  input  in_8,
  input  in_9,
  input  in_10,
  input  in_11,
  input  in_12,
  input  in_13,
  input  in_14,
  input  in_15,
  input  in_16,
  input  in_17,
  input  in_18,
  input  in_19
);

  wire ali_1_s1, ali_1_s2, ali_1_s3, ali_1_s4, ali_1_s5, blocos_1_m1, blocos_1_x1, blocos_1_x2, blocos_1_x3,
       blocos_1_x4, blocos_1_y1, blocos_1_y2, blocos_1_y3, blocos_1_y4, decodificador_1_f1,
       decodificador_1_f2, decodificador_1_f3, decodificador_1_f4, decodificador_1_f5, decodificador_1_f6,
       decodificador_1_f7, decodificador_1_g1, decodificador_1_g2, decodificador_1_g3, decodificador_1_g4,
       decodificador_1_g5, decodificador_1_g6, decodificador_1_g7, imparpar_1_i, imparpar_1_p, mult3_1_out_6;

  Blocos blocos_1 (
    .A1(in_1), .A2(in_2), .A3(in_3), .A4(in_4), .A5(in_5), .A6(in_6), .A7(in_7), .A8(in_8), .A9(in_9),
    .B1(in_11), .b2(in_12), .b3(in_13), .b4(in_14), .b5(in_15), .b6(in_16), .b7(in_17), .b8(in_18),
    .b9(in_19), .MaisMenos(in_10), .x1(blocos_1_x1), .x2(blocos_1_x2), .x3(blocos_1_x3), .x4(blocos_1_x4),
    .m1(blocos_1_m1), .y1(blocos_1_y1), .y2(blocos_1_y2), .y3(blocos_1_y3), .y4(blocos_1_y4));
  Ali ali_1 (
    .q1(blocos_1_x1), .q2(blocos_1_x2), .q3(blocos_1_x3), .q4(blocos_1_x4), .m(blocos_1_m1),
    .w1(blocos_1_y1), .w2(blocos_1_y2), .w3(blocos_1_y3), .w4(blocos_1_y4), .s1(ali_1_s1), .s2(ali_1_s2),
    .s3(ali_1_s3), .s4(ali_1_s4), .s5(ali_1_s5));
  LED led_1 (.in(imparpar_1_i));
  imparpar imparpar_1 (.e5(ali_1_s5), .i(imparpar_1_i), .p(imparpar_1_p));
  LED led_2 (.in(imparpar_1_p));
  Mult3 mult3_1 (
    .in_1(ali_1_s1), .in_2(ali_1_s2), .in_3(ali_1_s3), .in_4(ali_1_s4), .in_5(ali_1_s5), .out_6(mult3_1_out_6));
  decodificador decodificador_1 (
    .e1(ali_1_s1), .e2(ali_1_s2), .e3(ali_1_s3), .e4(ali_1_s4), .e5(ali_1_s5), .f4(decodificador_1_f4),
    .f3(decodificador_1_f3), .f2(decodificador_1_f2), .f1(decodificador_1_f1), .g1(decodificador_1_g1),
    .g2(decodificador_1_g2), .g3(decodificador_1_g3), .g4(decodificador_1_g4), .f5(decodificador_1_f5),
    .g5(decodificador_1_g5), .g6(decodificador_1_g6), .g7(decodificador_1_g7), .f7(decodificador_1_f7),
    .f6(decodificador_1_f6));
  LED led_3 (.in(mult3_1_out_6));
  _7_Segment_Display u_7_segment_display_1 (
    .g(decodificador_1_f1), .f(decodificador_1_f2), .a(decodificador_1_f3), .b(decodificador_1_f4),
    .e(decodificador_1_f5), .d(decodificador_1_f6), .c(decodificador_1_f7));  // open: dp
  _7_Segment_Display u_7_segment_display_2 (
    .g(decodificador_1_g1), .f(decodificador_1_g2), .a(decodificador_1_g3), .b(decodificador_1_g4),
    .e(decodificador_1_g5), .d(decodificador_1_g6), .c(decodificador_1_g7));  // open: dp

  // Notes on the sheet:
  //   impar
  //   par
  //   multiplo de 3
endmodule

module imparpar (
  input  e5,
  output i,
  output p
);

  _7404 u_7404_1 (.pin13(e5), .pin12(p));  // open: pin1, pin2, pin3, pin4, pin5, pin6, pin11, pin10, pin9, pin8

  assign i = e5;
endmodule
